# Fritzing sketch H1xyxy (saved by Fritzing 1.0.5)
breadboards: 1

parts:
  A1 = Waveshare rp2040-zero tht [package=THT]
  BPW32 = S1133 Si Photodiode [package="8mm Ceramic [THT]"]  # not connected
  RGB_SMD_LED1 = SMD RGB LED (WS2812) [package=5050]
  RGB_SMD_LED2 = SMD RGB LED (WS2812) [package=5050]
  RGB_SMD_LED3 = SMD RGB LED (WS2812) [package=5050]
  tY = Basic Servo
  bY = Basic Servo
  tX = Basic Servo
  bX = Basic Servo
  C1 = Capacitor Polarized [package=cpol-radial-1000uf-25v]  # not connected
  C2 = Capacitor Polarized [package=cpol-radial-1000uf-25v]  # not connected
  C3 = Capacitor Polarized [package=cpol-radial-1000uf-25v]
  C4 = Capacitor Polarized [package=cpol-radial-1000uf-25v]

nets:
  N1: A1.Pin_20, tY.pulse
  N2: A1.Pin_21, tX.pulse
  N3: A1.Pin_22, bY.pulse
  N4: A1.Pin_23, bX.pulse
  N5: RGB_SMD_LED1.DOut, RGB_SMD_LED2.DIn
  VCC: RGB_SMD_LED1.VCC, RGB_SMD_LED2.VCC, RGB_SMD_LED3.VCC, tY.vcc, bY.vcc, tX.vcc, bX.vcc, C3.-, C4.-
  N6: RGB_SMD_LED2.DOut, RGB_SMD_LED3.DIn
  GND: tY.gnd, bY.gnd, tX.gnd, bX.gnd, C3.+, C4.+

custom parts:
  Waveshare rp2040-zero tht: .RP2040-Zero, A Low-Cost, High-Performance Pico-Like MCU Board Based On Raspberry Pi Microcontroller RP2040. This varant is THT without the extra connections.
