# Fritzing sketch TentacleV1 (saved by Fritzing 1.0.5)
breadboards: 1

parts:
  M4 = Basic Servo
  M1 = Basic Servo
  M2 = Basic Servo
  M3 = Basic Servo
  Part1 = Arduino Uno (Rev3)
  C3 = Capacitor Polarized [package=cpol-radial-10uf-25v]
  Part2 = Breadboard Power Supply Board SMD
  C4 = Capacitor Polarized [package=cpol-radial-10uf-25v]
  Part3 = Thumb Joystick
  C2 = Capacitor Polarized [package=cpol-radial-10uf-25v]
  C1 = Capacitor Polarized [package=cpol-radial-10uf-25v]

nets:
  GND: M4.gnd, M1.gnd, M2.gnd, M3.gnd, Part1.GND, C3.-, Part2.GND, C4.-, Part3.GND, C2.-, C1.-
  VCC: M4.vcc, M1.vcc, M2.vcc, M3.vcc, C3.+, Part2.VCC, C4.+, C2.+, C1.+
  N1: M4.pulse, Part1.D9_PWM
  N2: M1.pulse, Part1.D3_PWM
  N3: M2.pulse, Part1.D5_PWM
  N4: M3.pulse, Part1.D6_PWM
  N5: Part1.A0, Part3.VERT
  N6: Part1.A1, Part3.HORZ
  5V: Part1.5V, Part3.VCC
